# Fritzing sketch robot_circuit (saved by Fritzing 0.8.7b)
breadboards: 1

parts:
  IC1 = L293D [package=THT]
  IC2 = L293D [package=THT]
  M1 = DC Motor
  M2 = DC Motor
  M3 = DC Motor
  M4 = DC Motor
  VCC1 = Battery block 9V

nets:
  N1: IC1.Out_1_(_Controlled_by_Enable_1_), M1.pin_2
  N2: IC1.0V, IC2.0V, VCC1.-
  N3: IC1.Out_2_(_Controlled_by_Enable_1_), M1.pin_1
  N4: IC1.+Vmotor, IC1.+V, IC2.+Vmotor, IC2.+V, VCC1.+
  N5: IC1.Out_3_(_Controlled_by_Enable_2_), M2.pin_2
  N6: IC1.Out_4_(_Controlled_by_Enable_2_), M2.pin_1
  N7: IC2.Out_1_(_Controlled_by_Enable_1_), M3.pin_2
  N8: IC2.Out_2_(_Controlled_by_Enable_1_), M3.pin_1
  N9: IC2.Out_3_(_Controlled_by_Enable_2_), M4.pin_2
  N10: IC2.Out_4_(_Controlled_by_Enable_2_), M4.pin_1

notes:
  PIN 23
  PIN 24
  PIN 25
  PIN 22
  PIN 27
  PIN 17
  PIN 16
  PIN 12
  PIN 1
  PIN 26
  PIN 5
  PIN 6
